# Fritzing sketch UNOandHC05 (saved by Fritzing 0.8.7b)
breadboards: 1

parts:
  Part1 = Arduino Uno (Rev3)
  LED1 = LED - 5mm [color="Red (633nm)" package="5 mm [THT]"]

nets:
  N1: Part1.D13/SCK, LED1.anode
  N2: Part1.GND, LED1.cathode
