# Fritzing sketch setTime (saved by Fritzing 0.8.7b)
breadboards: 1

parts:
  Part1 = Arduino Uno (Rev3) - ICSP
  Part2 = Real Time Clock Module - DS1307 RTC Breakout Board

nets:
  N1: Part1.A4/SDA, Part2.SCL
  N2: Part1.A5/SCL, Part2.SDA
  5V: Part1.5V, Part2.5V
  GND: Part1.GND, Part2.GND
